# Fritzing sketch printing_PCB (saved by Fritzing 0.9.3b)
circuit board: 6.46404cm x 2.96893cm
breadboards: 1

parts:
  J1 = female pin header, 4 pins [form="♀ (female)"]
  J2 = female pin header, 7 pins [form="♀ (female)"]

nets:
  N1: J1.pin1, J2.pin1
  N2: J1.pin2, J2.pin2
  N3: J1.pin3, J2.pin6
  N4: J1.pin4, J2.pin7

notes:
  Vin
  GND
  SDA
  SCL
  Harsimran Saini
  TSL2561
